# Fritzing sketch 47a-KikkerkokenInput (saved by Fritzing 1.0.6)
circuit board: 8.46667cm x 5.64444cm
breadboards: 1

parts:
  Lestrip_Knoppen = SMD RGB LED (WS2812) [package=5050]
  Ledstrip_Rest = SMD RGB LED (WS2812) [package=5050]
  4a = Square Pushbutton
  3b = Square Pushbutton
  3a = Square Pushbutton
  2b = Square Pushbutton
  2a = Square Pushbutton
  1b = Square Pushbutton
  1a = Square Pushbutton
  Start = Square Pushbutton
  R4 = Resistor [tolerance=±5% resistance=470 package="0603 [SMD]"]
  R5 = Resistor [tolerance=±5% resistance=470 package="0603 [SMD]"]
  1000uF_25V = Capacitor Polarized [package=panasonic_g]
  1000uF_25V_2 = Capacitor Polarized [package=panasonic_g]
  4b = Square Pushbutton
  part = Arduino Micro (Rev3)

nets:
  N1: Lestrip_Knoppen.DIn, R4.Pin_1
  VCC: Lestrip_Knoppen.VCC, Ledstrip_Rest.VCC, 1000uF_25V.+, 1000uF_25V_2.+
  0V: Lestrip_Knoppen.VSS, Ledstrip_Rest.VSS, 1000uF_25V.-, 1000uF_25V_2.-, part.GND
  N2: Ledstrip_Rest.DIn, R5.Pin_1
  N3: 4a.leg0, part.D5_PWM
  N4: 3b.leg0, part.D6_PWM/A7
  N5: 3a.leg0, part.D7
  N6: 2b.leg0, part.D8_PWM/A8
  N7: 2a.leg0, part.D9_PWM/A9
  N8: 1b.leg0, part.D10_PWM/A10
  N9: 1a.leg0, part.D11_PWM
  N10: 1a.leg1, Start.leg1, 4b.leg1
  N11: Start.leg0, part.D2/SDA
  N12: R4.Pin_0, part.A1
  N13: R5.Pin_0, part.A0
  N14: 4b.leg0, part.D4_PWM/A6
  5V: part.5V

notes:
  Wit
  Blauw
  Grijs
  Bruin
  Paars
  Roze
  Geel
  Groen
  Oranje
