# Fritzing sketch 47b-KikkerkokenOutput (saved by Fritzing 1.0.6)
circuit board: 12.5227cm x 9.27753cm
breadboards: 1

parts:
  Strip_1_-_Knoppen = SMD RGB LED (WS2812) [package=5050]
  Ledstrip_2_-_Pannetjes = SMD RGB LED (WS2812) [package=5050]
  5 = Square Pushbutton
  4 = Square Pushbutton
  3 = Square Pushbutton
  2 = Square Pushbutton
  1 = Square Pushbutton
  1000uF_25V = Capacitor Polarized [package=panasonic_g]
  1000uF_25V_2 = Capacitor Polarized [package=panasonic_g]
  R5 = Resistor [tolerance=±5% resistance=470 power=0.25W package=THT]
  R4 = Resistor [tolerance=±5% resistance=470 power=0.25W package=THT]
  BUBBELS_EN_STOOM = SMD RGB LED (WS2812) [package=5050]
  Deze_strip_wil_ook_een_condensator_en_voeding = Arduino Micro (Rev3)
  R6 = Resistor [tolerance=±5% resistance=470 power=0.25W package=THT]

nets (from the schematic view):
  N1: Strip_1_-_Knoppen.DIn, R4.Pin_1
  5V: Strip_1_-_Knoppen.VCC, Ledstrip_2_-_Pannetjes.VCC, 1000uF_25V.+, 1000uF_25V_2.+, Deze_strip_wil_ook_een_condensator_en_voeding.VIN
  0V: Strip_1_-_Knoppen.VSS, 5.leg1, 4.leg1, 3.leg1, 2.leg1, 1.leg1, 1000uF_25V_2.-, Deze_strip_wil_ook_een_condensator_en_voeding.GND
  N2: Ledstrip_2_-_Pannetjes.DIn, R5.Pin_1
  N3: Ledstrip_2_-_Pannetjes.VSS, 1000uF_25V.-
  N4: 5.leg0, Deze_strip_wil_ook_een_condensator_en_voeding.D7
  N5: 4.leg0, Deze_strip_wil_ook_een_condensator_en_voeding.D8_PWM/A8
  N6: 3.leg0, Deze_strip_wil_ook_een_condensator_en_voeding.D9_PWM/A9
  N7: 2.leg0, Deze_strip_wil_ook_een_condensator_en_voeding.D10_PWM/A10
  N8: 1.leg0, Deze_strip_wil_ook_een_condensator_en_voeding.D11_PWM
  N9: R5.Pin_0, Deze_strip_wil_ook_een_condensator_en_voeding.A1
  N10: R4.Pin_0, Deze_strip_wil_ook_een_condensator_en_voeding.A0
  N11: BUBBELS_EN_STOOM.DIn, R6.Pin_0
  N12: Deze_strip_wil_ook_een_condensator_en_voeding.A2, R6.Pin_1
